# Fritzing sketch Untitled Sketch (saved by Fritzing 0.9.3b)
breadboards: 1

parts:
  SW1 = ENCODER_RGB_CA [package=encoder_led_3]
  Componente1 = Arduino Mega 2560 (Rev3)
  Q1 = pnp-Powertransistor [package="TO220 [THT]"]
  LED1 = Super Flux RGB LED (com. cathode)
  LED2 = Super Flux RGB LED (com. cathode)  # not connected
  LED3 = Super Flux RGB LED (com. cathode)  # not connected
  LED4 = Super Flux RGB LED (com. cathode)  # not connected
  LED5 = Super Flux RGB LED (com. cathode)  # not connected
  LED6 = Super Flux RGB LED (com. cathode)  # not connected
  LED7 = Super Flux RGB LED (com. cathode)  # not connected
  LED8 = Super Flux RGB LED (com. cathode)  # not connected
  LED9 = Super Flux RGB LED (com. cathode)  # not connected
  LED10 = Super Flux RGB LED (com. cathode)  # not connected
  LED11 = Super Flux RGB LED (com. cathode)  # not connected
  LED12 = Super Flux RGB LED (com. cathode)  # not connected
  Power_plug1 = Power plug

nets:
  N1: SW1.-R, Componente1.5V
  N2: SW1.-G, Componente1.A0
  N3: SW1.SW, Componente1.D6_PWM
  N4: Componente1.D8_PWM, Q1.base
  GND: Componente1.GND, Q1.emitter, Power_plug1.GND
  N5: Q1.collector, LED1.common_cathode
  N6: LED1.red_anode, Power_plug1.VCC
